// Logisim project 3-bit Full Adder.circ as structural Verilog: 1 circuit, main circuit Full Adder
module Full_Adder (
  input  A_2,
  input  A_1,
  input  A_0,
  input  B_2,
  input  B_1,
  input  B_0,
  output S_1,
  output S_2,
  output S_0
);

  wire and_1_out, and_2_out, and_3_out, and_5_out, and_6_out, nand_1_out, nand_2_out, nand_3_out, nand_4_out,
       nand_5_out, or_1_out, or_2_out, or_3_out, or_4_out, or_5_out, or_6_out;

  and and_1 (and_1_out, A_0, B_0);
  nand nand_1 (nand_1_out, A_1, B_1);
  or or_1 (or_1_out, B_1, A_1);
  nand nand_2 (nand_2_out, A_2, B_2);
  or or_2 (or_2_out, B_2, A_2);
  nand nand_3 (nand_3_out, A_0, B_0);
  or or_3 (or_3_out, B_0, A_0);
  and and_2 (and_2_out, nand_1_out, or_1_out);
  and and_3 (and_3_out, nand_2_out, or_2_out);
  and and_4 (S_1, nand_3_out, or_3_out);
  and and_5 (and_5_out, and_2_out, and_1_out);
  and and_6 (and_6_out, A_1, B_1);
  nand nand_4 (nand_4_out, and_3_out, or_6_out);
  or or_4 (or_4_out, or_6_out, and_3_out);
  nand nand_5 (nand_5_out, and_2_out, and_1_out);
  or or_5 (or_5_out, and_1_out, and_2_out);
  or or_6 (or_6_out, and_5_out, and_6_out);
  and and_7 (S_2, nand_4_out, or_4_out);
  and and_8 (S_0, nand_5_out, or_5_out);

  // Notes on the sheet:
  //   Число А
  //   Число В
  //   C_in_1
  //   C_in_2
  //   Полный сумматор (Full Adder) двух 3-битных входов.
  //   C_out_0
  //   Голенских Н.А.
  //   C_out_1
  //   СУММА
endmodule
